# Fritzing sketch Diagrama (saved by Fritzing 0.9.3b)
breadboards: 1

parts:
  KY-1 = Keyes Relay [package=THT]
  Componente1 = Arduino Uno (Rev3)

nets:
  N1: KY-1.signal, Componente1.D7
  N2: KY-1.power, Componente1.5V
  N3: KY-1.ground, Componente1.GND

custom parts:
  Keyes Relay: The Keyes 5V relay module is suitable for SCM development, home appliance control. It uses a 5V~12V TIL control signal which can control DC / AC signal.
